// Logisim project counter.circ as structural Verilog: 1 circuit, main circuit main
module main (
);

  wire and_1_out, and_2_out, and_3_out, and_4_out, and_5_out, and_6_out, button_1_out;
  wire [3:0] t_ff_1_q, t_ff_5_q;

  Button button_1 (.out(button_1_out));
  and and_1 (and_1_out, t_ff_1_q[0], t_ff_1_q[1]);
  and and_2 (and_2_out, t_ff_1_q[2], and_1_out);
  and and_3 (and_3_out, and_2_out, t_ff_1_q[3]);
  and and_4 (and_4_out, and_3_out, t_ff_5_q[0]);
  and and_5 (and_5_out, and_4_out, t_ff_5_q[1]);
  and and_6 (and_6_out, and_5_out, t_ff_5_q[2]);
  T_Flip_Flop t_ff_1 (.clk(button_1_out), .T(button_1_out), .Q(t_ff_1_q[0]));  // open: Qn, preset, reset
  T_Flip_Flop t_ff_2 (.clk(button_1_out), .T(t_ff_1_q[0]), .Q(t_ff_1_q[1]));  // open: Qn, preset, reset
  T_Flip_Flop t_ff_3 (.clk(button_1_out), .T(and_1_out), .Q(t_ff_1_q[2]));  // open: Qn, preset, reset
  T_Flip_Flop t_ff_4 (.clk(button_1_out), .T(and_2_out), .Q(t_ff_1_q[3]));  // open: Qn, preset, reset
  T_Flip_Flop t_ff_5 (.clk(button_1_out), .T(and_3_out), .Q(t_ff_5_q[0]));  // open: Qn, preset, reset
  T_Flip_Flop t_ff_6 (.clk(button_1_out), .T(and_4_out), .Q(t_ff_5_q[1]));  // open: Qn, preset, reset
  T_Flip_Flop t_ff_7 (.clk(button_1_out), .T(and_5_out), .Q(t_ff_5_q[2]));  // open: Qn, preset, reset
  T_Flip_Flop t_ff_8 (.clk(button_1_out), .T(and_6_out), .Q(t_ff_5_q[3]));  // open: Qn, preset, reset
  Hex_Digit_Display hex_digit_display_1 (.value(t_ff_5_q));  // open: dp
  Hex_Digit_Display hex_digit_display_2 (.value(t_ff_1_q));  // open: dp
endmodule
