// Logisim project Lista04_NOR_Universal.circ as structural Verilog: 1 circuit, main circuit main
module main (
);

  wire button_1_out, button_2_out, button_3_out, nor_1_out, nor_2_out, nor_3_out, nor_4_out;
  wire [1:0] slider_1_out;

  Button button_1 (.out(button_1_out));
  Button button_2 (.out(button_2_out));
  Button button_3 (.out(button_3_out));
  nor nor_1 (nor_1_out, button_1_out, button_1_out);
  Slider #(.width(2), .value('h3)) slider_1 (.out(slider_1_out));
  LED led_1 (.in(nor_1_out));
  nor nor_2 (nor_2_out, slider_1_out[0], slider_1_out[0]);
  nor nor_3 (nor_3_out, slider_1_out[1], slider_1_out[1]);
  LED led_2 (.in(nor_4_out));
  nor nor_4 (nor_4_out, nor_2_out, nor_3_out);
endmodule
