// Logisim project SomadorCIs.circ as structural Verilog: 1 circuit, main circuit main
module main (
);

  wire n7432_1_pin1, n7432_1_pin2, n7432_1_pin3, n7432_1_pin4, n7432_1_pin5, n7432_1_pin6, n7432_1_pin9,
       n7432_1_pin10, n7486_1_pin5, n7486_1_pin8, n7486_1_pin9, n7486_1_pin10, n7486_1_pin12, n7486_1_pin13,
       n7486_2_pin4, n7486_2_pin5, n7486_2_pin9, n7486_2_pin10, n7486_2_pin12, n7486_2_pin13;
  wire [0:0] n7432_1_pin8;
  wire [3:0] n7486_2_pin8;

  Hex_Digit_Display hex_digit_display_1 (.value({3'b000, n7432_1_pin8[0]}));  // open: dp
  Hex_Digit_Display hex_digit_display_2 (.value(n7486_2_pin8));  // open: dp
  _7432 u_7432_1 (
    .pin1(n7432_1_pin1), .pin2(n7432_1_pin2), .pin3(n7432_1_pin3), .pin4(n7432_1_pin4), .pin5(n7432_1_pin5),
    .pin6(n7432_1_pin6), .pin10(n7432_1_pin10), .pin9(n7432_1_pin9), .pin8(n7432_1_pin8[0]));  // open: pin13, pin12, pin11
  _7486 u_7486_1 (
    .pin4(n7432_1_pin3), .pin5(n7486_1_pin5), .pin6(n7486_2_pin8[3]), .pin13(n7486_1_pin13),
    .pin12(n7486_1_pin12), .pin11(n7486_1_pin5), .pin10(n7486_1_pin10), .pin9(n7486_1_pin9),
    .pin8(n7486_1_pin8));  // open: pin1, pin2, pin3
  _7408 u_7408_1 (
    .pin4(n7432_1_pin3), .pin5(n7486_1_pin5), .pin6(n7432_1_pin10), .pin13(n7486_1_pin13),
    .pin12(n7486_1_pin12), .pin11(n7432_1_pin9), .pin10(n7486_1_pin10), .pin9(n7486_1_pin9),
    .pin8(n7432_1_pin1));  // open: pin1, pin2, pin3
  _7486 u_7486_2 (
    .pin1(n7432_1_pin6), .pin2(n7486_1_pin8), .pin3(n7486_2_pin8[2]), .pin4(n7486_2_pin4),
    .pin5(n7486_2_pin5), .pin6(n7486_2_pin8[1]), .pin13(n7486_2_pin13), .pin12(n7486_2_pin12),
    .pin11(n7486_2_pin4), .pin10(n7486_2_pin10), .pin9(n7486_2_pin9), .pin8(n7486_2_pin8[0]));
  _7408 u_7408_2 (
    .pin1(n7432_1_pin6), .pin2(n7486_1_pin8), .pin3(n7432_1_pin2), .pin4(n7486_2_pin4), .pin5(n7486_2_pin5),
    .pin6(n7432_1_pin5), .pin13(n7486_2_pin13), .pin12(n7486_2_pin12), .pin11(n7432_1_pin4),
    .pin10(n7486_2_pin10), .pin9(n7486_2_pin9), .pin8(n7486_2_pin5));
  // DipSwitch dipswitch_1: pin names not known; wires that end beside it: n7486_1_pin12, n7486_1_pin9, n7486_2_pin13
  // DipSwitch dipswitch_2: pin names not known; wires that end beside it: n7486_2_pin9, n7486_1_pin13, n7486_1_pin10, n7486_2_pin12, n7486_2_pin10

  // Notes on the sheet:
  //   OUTPUT
endmodule
